# Fritzing sketch otamatone_breakout (saved by Fritzing 0.9.3b)
circuit board: 3.76046cm x 1.82767cm

parts:
  C7 = Tantalum Capacitor [capacitance=10µF package="B 3528 [SMD, tantalum]"]
  C5 = Tantalum Capacitor [capacitance=10µF package="B 3528 [SMD, tantalum]"]
  C6 = Tantalum Capacitor [capacitance=10µF package="B 3528 [SMD, tantalum]"]
  C4 = Ceramic Capacitor [capacitance=100nF package="0805 [SMD, multilayer]"]
  C3 = Ceramic Capacitor [capacitance=100nF package="0805 [SMD, multilayer]"]
  R12 = Resistor [tolerance=±5% resistance=47k package="0805 [SMD]"]
  R6 = Resistor [tolerance=±5% resistance=47k package="0805 [SMD]"]
  R3 = Resistor [tolerance=±5% resistance=62k package="0805 [SMD]"]
  R2 = Resistor [tolerance=±5% resistance=10k package="0805 [SMD]"]
  R1 = Resistor [tolerance=±5% resistance=10k package="0805 [SMD]"]
  R5 = Resistor [tolerance=±5% resistance=10k package="0805 [SMD]"]
  R8 = Resistor [tolerance=±5% resistance=47k package="0805 [SMD]"]
  10k = Resistor [tolerance=±5% resistance=10k package="0805 [SMD]"]
  R4 = Resistor [tolerance=±5% resistance=10k package="0805 [SMD]"]
  R9 = Resistor [tolerance=±5% resistance=2.2k package="0805 [SMD]"]
  R13 = Resistor [tolerance=±5% resistance=47k package="0805 [SMD]"]
  C2 = Ceramic Capacitor [capacitance=100nF package="0805 [SMD, multilayer]"]
  Line_Out = male pin header, 2 pins [form="♂ (male)"]
  Line_In = male pin header, 3 pins [form="♂ (male)"]
  Neck = male pin header, 2 pins [form="♂ (male)"]
  Buttons = male pin header, 3 pins [form="♂ (male)"]
  OLED = male pin header, 4 pins [form="♂ (male)"]
  J1 = male pin header, 14 pins [form="♂ (male)"]
  Switch = male pin header, 3 pins [form="♂ (male)"]
  Volume = male pin header, 3 pins [form="♂ (male)"]
  J2 = male pin header, 3 pins [form="♂ (male)"]

nets:
  N1: C7.-, R13.Pin_0, Line_In.pin2
  INR: C7.+, R12.Pin_0, J1.pin10
  N2: C5.-, R8.Pin_0, Line_In.pin1
  INL: C5.+, R6.Pin_0, J1.pin11
  AGND: C6.-, C4.1, C3.0, R3.Pin_1, R8.Pin_1, R9.Pin_1, R13.Pin_1, Line_Out.pin2, Line_In.pin3, J1.pin2, Volume.pin3
  N3: C6.+, R12.Pin_1, R6.Pin_1, 10k.Pin_1, R9.Pin_0
  VPOT: C4.0, J1.pin4, Volume.pin2
  NECK: C3.1, R3.Pin_0, Neck.pin2, J1.pin7
  SDA: R2.Pin_0, OLED.pin1, J1.pin9
  3v3: R2.Pin_1, R1.Pin_1, 10k.Pin_0, Neck.pin1, Buttons.pin3, J1.pin3, Volume.pin1
  SCL: R1.Pin_0, OLED.pin2, J1.pin8
  BT0: R5.Pin_0, Buttons.pin2, J1.pin5
  DGND: R5.Pin_1, R4.Pin_1, OLED.pin3, J2.pin1
  BT1: R4.Pin_0, Buttons.pin1, J1.pin6
  DAC: C2.0, J2.pin3
  N4: C2.1, Line_Out.pin1
  5v0: OLED.pin4, J1.pin1, Switch.pin3
  A12: J1.pin12
  A14: J1.pin13
  A13: J1.pin14
  Vin: Switch.pin1, Switch.pin2
  PRGM: J2.pin2

notes:
  <line in [l/r/g]
  line out [+-]
  neck[-/+]
  oled [sda/scl/g/5v]
  btn [0/1/3v]
  volume pot [+w-]>
  sw [vin/-/+]
  Otamatone Breakout 1.0
  hackaday.io/evan
